// Logisim project problem3.circ as structural Verilog
module main (
  input  [2:0] in_1
);

  wire [7:0] seg7_letters_1_display;

  seg7_letters seg7_letters_1 (.sel(in_1), .display(seg7_letters_1_display));
  _7_Segment_Display u_7_segment_display_1 (
    .g(seg7_letters_1_display[1]), .f(seg7_letters_1_display[2]), .a(seg7_letters_1_display[7]),
    .b(seg7_letters_1_display[6]), .e(seg7_letters_1_display[3]), .d(seg7_letters_1_display[4]),
    .c(seg7_letters_1_display[5]), .dp(seg7_letters_1_display[0]));
endmodule

// VHDL entity seg7_letters, as the project stores it:
library ieee;
use ieee.std_logic_1164.all;

entity seg7_letters is
    port(
        sel : in std_logic_vector(2 downto 0);
        display : out std_logic_vector(7 downto 0)
    );
end entity seg7_letters;

architecture bhv of seg7_letters is
begin
    process(sel)
    begin
        case sel is
            when "000" => display <= "11111010"; -- a
            when "001" => display <= "00111110"; -- b
            when "010" => display <= "00011010"; -- c
            when "011" => display <= "01111010"; -- d
            when "100" => display <= "10001110"; -- f
            when "101" => display <= "11110110"; -- g
            when others => display <= "00000000";
        end case;
    end process;
end architecture bhv;
